# Fritzing sketch attiny13_alarm (saved by Fritzing 0.9.1b)
circuit board: 8.46667cm x 5.64444cm
breadboards: 1

parts:
  IC1 = IC, DIP package, 8 pins [chip_label=ATTINY13]
  J1 = AVR ISP 6 Pin [package=2x3-ns]
  J2 = Piezo Speaker
  R1 = Resistor [tolerance=±5% resistance=1k package=THT]
  S1 = Pushbutton [package="[THT]"]
  R2 = Resistor [tolerance=±5% resistance=10k package=THT]
  Q1 = TRANSISTOR_NPN [part_number=s9013 package=to-92-ammo]
  R3 = Resistor [tolerance=±5% resistance=1k package=THT]
  R4 = Resistor [tolerance=±5% resistance=270 package=THT]
  PIR1 = PIR sensor
  LED1 = LEDs [package=led10mm]
  R5 = Resistor [tolerance=±5% resistance=330 package=THT]
  U1 = RELAY [package=relay-jzc]
  Q2 = TRANSISTOR_NPN [package=to-92-ammo]
  R6 = Resistor [tolerance=±5% resistance=1k package=THT]
  IC2 = Voltage Regulator [part_number=7805 package=to-220-alt]
  C1 = Electrolytic Capacitor [capacitance=0.33µF voltage=16V package="0605 [SMD, electrolytic]"]
  C2 = Electrolytic Capacitor [capacitance=0.1µF package="0605 [SMD, electrolytic]"]

nets:
  N1: IC1.pin1, J1.5
  N2: IC1.pin2, R6.Pin_1
  N3: IC1.pin3, PIR1.VDD, R5.Pin_0
  N4: IC1.pin4, J1.6, J2.pin2, R2.Pin_1, Q1.E, PIR1.GND, LED1.C, U1.COIL1, Q2.C
  N5: IC1.pin5, Q1.C, R3.Pin_1
  N6: IC1.pin6, J1.1, R1.Pin_0
  N7: IC1.pin7, J1.3, S1.Pin_1, S1.Pin_2, R2.Pin_0
  N8: IC1.pin8, J1.2, S1.Pin_3, S1.Pin_4, R3.Pin_0, IC2.OUT, C2.+
  N9: J2.pin1, R1.Pin_1
  N10: Q1.B, R4.Pin_1
  N11: R4.Pin_0, PIR1.SIG
  N12: LED1.A, R5.Pin_1
  N13: U1.COIL2, Q2.E
  +12V/12V: U1.MAIN, IC2.IN, C1.+
  N14: Q2.B, R6.Pin_0
  GND/GND_: IC2.GND, C1.-, C2.-

notes:
  12V 120db ALARM
  attiny13-alarm, Small domestic PIR intrusion alarm, 1
